# Fritzing sketch ISBN_Verifier (saved by Fritzing 0.9.3b)
breadboards: 2

parts:
  Nokia_5110_LCD_Module1 = Nokia 5110 LCD basado en PCD8544
  Keypad4x1 = Keypad Membran 4x4
  Part1 = Arduino Nano (Rev3.0)
  R2 = Resistor [tolerance=±5% resistance=220 package="2010 [SMD]"]
  R3 = Resistor [tolerance=±5% resistance=220 package="2010 [SMD]"]
  R4 = Resistor [tolerance=±5% resistance=220 package="2010 [SMD]"]
  R5 = Resistor [tolerance=±5% resistance=220 package="2010 [SMD]"]
  R6 = Resistor [tolerance=±5% resistance=220 package="2010 [SMD]"]

nets:
  VCC: Nokia_5110_LCD_Module1.VCC, Nokia_5110_LCD_Module1.LIGHT, Part1.3V3
  GND: Nokia_5110_LCD_Module1.GND, Part1.GND
  N1: Nokia_5110_LCD_Module1.CE, R5.Pin_0
  N2: Nokia_5110_LCD_Module1.RST, R6.Pin_0
  N3: Nokia_5110_LCD_Module1.DC, R4.Pin_0
  N4: Nokia_5110_LCD_Module1.DIN, R3.Pin_0
  N5: Nokia_5110_LCD_Module1.CLK, R2.Pin_0
  N6: Keypad4x1.Pin1, Part1.A0
  N7: Keypad4x1.Pin2, Part1.A1
  N8: Keypad4x1.Pin3, Part1.A2
  N9: Keypad4x1.Pin4, Part1.A3
  N10: Keypad4x1.Pin5, Part1.A4
  N11: Keypad4x1.Pin6, Part1.A5
  N12: Keypad4x1.Pin7, Part1.A6
  N13: Keypad4x1.Pin8, Part1.A7
  N14: Part1.D8, R2.Pin_1
  N15: Part1.D9, R3.Pin_1
  N16: Part1.D10, R4.Pin_1
  N17: Part1.D11/MOSI, R6.Pin_1
  N18: Part1.D12/MISO, R5.Pin_1

notes:
  Arduino Nano 33 IoT
  Pinout

custom parts:
  Nokia 5110 LCD basado en PCD8544: Módulo Nokia 5110 LCD basado en el controlador PCD8544. Versión de 8 pines (sólo entrada).
  Keypad Membran 4x4: Membrane Keypad 4x4 Matrix
